// Digital circuit 32_byte_ram.dig as structural Verilog
module _32_byte_ram (
  input  [7:0] Bus,
  input  [4:0] Addr,
  input  Wr,
  input  Clk,
  input  En,
  output [7:0] Out
);

  wire demultiplexer_1_out_0, demultiplexer_1_out_1, demultiplexer_1_out_2, demultiplexer_1_out_3;
  wire [7:0] _8_byte_ram_1_out, _8_byte_ram_2_out, _8_byte_ram_3_out, _8_byte_ram_4_out, multiplexer_1_out;

  Demultiplexer #(.Selector_Bits(2)) demultiplexer_1 (
    .sel(Addr[4:3]), .in(Wr), .out_0(demultiplexer_1_out_0), .out_1(demultiplexer_1_out_1),
    .out_2(demultiplexer_1_out_2), .out_3(demultiplexer_1_out_3));
  _8_byte_ram _8_byte_ram_1 (
    .Addr(Addr[2:0]), .Clk(Clk), .Wr(demultiplexer_1_out_0), .En(En), .Bus(Bus), .Out(_8_byte_ram_1_out));
  _8_byte_ram _8_byte_ram_2 (
    .Addr(Addr[2:0]), .Clk(Clk), .Wr(demultiplexer_1_out_1), .En(En), .Bus(Bus), .Out(_8_byte_ram_2_out));
  _8_byte_ram _8_byte_ram_3 (
    .Addr(Addr[2:0]), .Clk(Clk), .Wr(demultiplexer_1_out_2), .En(En), .Bus(Bus), .Out(_8_byte_ram_3_out));
  _8_byte_ram _8_byte_ram_4 (
    .Addr(Addr[2:0]), .Clk(Clk), .Wr(demultiplexer_1_out_3), .En(En), .Bus(Bus), .Out(_8_byte_ram_4_out));
  Multiplexer #(.Selector_Bits(2), .Bits(8)) multiplexer_1 (
    .sel(Addr[4:3]), .in_0(_8_byte_ram_1_out), .in_1(_8_byte_ram_2_out), .in_2(_8_byte_ram_3_out),
    .in_3(_8_byte_ram_4_out), .out(multiplexer_1_out));
  assign Out = En ? multiplexer_1_out : 8'bz;  // Driver driver_1
endmodule
