// Digital circuit 8_bit_reg.dig as structural Verilog
module _8_bit_reg (
  input  Load,
  input  Clk,
  input  D7,
  input  D6,
  input  D5,
  input  D4,
  input  D3,
  input  D2,
  input  D1,
  input  D0,
  output Q7,
  output Q6,
  output Q5,
  output Q4,
  output Q3,
  output Q2,
  output Q1,
  output Q0
);

  _1_bit_reg _1_bit_reg_1 (.Load(Load), .D(D0), .Clk(Clk), .Q(Q0));
  _1_bit_reg _1_bit_reg_2 (.Load(Load), .D(D1), .Clk(Clk), .Q(Q1));
  _1_bit_reg _1_bit_reg_3 (.Load(Load), .D(D2), .Clk(Clk), .Q(Q2));
  _1_bit_reg _1_bit_reg_4 (.Load(Load), .D(D3), .Clk(Clk), .Q(Q3));
  _1_bit_reg _1_bit_reg_5 (.Load(Load), .D(D4), .Clk(Clk), .Q(Q4));
  _1_bit_reg _1_bit_reg_6 (.Load(Load), .D(D5), .Clk(Clk), .Q(Q5));
  _1_bit_reg _1_bit_reg_7 (.Load(Load), .D(D6), .Clk(Clk), .Q(Q6));
  _1_bit_reg _1_bit_reg_8 (.Load(Load), .D(D7), .Clk(Clk), .Q(Q7));
endmodule
