// Digital circuit 8_byte_ram.dig as structural Verilog
module _8_byte_ram (
  input  [2:0] Addr,
  input  Clk,
  input  Wr,
  input  En,
  input  [7:0] Bus,
  output [7:0] Out
);

  wire demultiplexer_1_out_0, demultiplexer_1_out_1, demultiplexer_1_out_2, demultiplexer_1_out_3,
       demultiplexer_1_out_4, demultiplexer_1_out_5, demultiplexer_1_out_6, demultiplexer_1_out_7;
  wire [7:0] multiplexer_1_out, register_1_q, register_2_q, register_3_q, register_4_q, register_5_q,
       register_6_q, register_7_q, register_8_q;

  Demultiplexer #(.Selector_Bits(3)) demultiplexer_1 (
    .sel(Addr), .in(Wr), .out_0(demultiplexer_1_out_0), .out_1(demultiplexer_1_out_1),
    .out_2(demultiplexer_1_out_2), .out_3(demultiplexer_1_out_3), .out_4(demultiplexer_1_out_4),
    .out_5(demultiplexer_1_out_5), .out_6(demultiplexer_1_out_6), .out_7(demultiplexer_1_out_7));
  Register #(.Bits(8)) register_1 (.D(Bus), .C(Clk), .en(demultiplexer_1_out_0), .Q(register_1_q));
  Register #(.Bits(8)) register_2 (.D(Bus), .C(Clk), .en(demultiplexer_1_out_1), .Q(register_2_q));
  Register #(.Bits(8)) register_3 (.D(Bus), .C(Clk), .en(demultiplexer_1_out_2), .Q(register_3_q));
  Register #(.Bits(8)) register_4 (.D(Bus), .C(Clk), .en(demultiplexer_1_out_3), .Q(register_4_q));
  Register #(.Bits(8)) register_5 (.D(Bus), .C(Clk), .en(demultiplexer_1_out_4), .Q(register_5_q));
  Register #(.Bits(8)) register_6 (.D(Bus), .C(Clk), .en(demultiplexer_1_out_5), .Q(register_6_q));
  Register #(.Bits(8)) register_7 (.D(Bus), .C(Clk), .en(demultiplexer_1_out_6), .Q(register_7_q));
  Register #(.Bits(8)) register_8 (.D(Bus), .C(Clk), .en(demultiplexer_1_out_7), .Q(register_8_q));
  Multiplexer #(.Selector_Bits(3), .Bits(8)) multiplexer_1 (
    .sel(Addr), .in_0(register_1_q), .in_1(register_2_q), .in_2(register_3_q), .in_3(register_4_q),
    .in_4(register_5_q), .in_5(register_6_q), .in_6(register_7_q), .in_7(register_8_q),
    .out(multiplexer_1_out));
  assign Out = En ? multiplexer_1_out : 8'bz;  // Driver driver_1
endmodule
