// Digital circuit ALU.dig as structural Verilog
module ALU (
  input  Sub,
  input  A7,
  input  A6,
  input  A5,
  input  A4,
  input  A3,
  input  A2,
  input  A1,
  input  A0,
  input  B7,
  input  B6,
  input  B5,
  input  B4,
  input  B3,
  input  B2,
  input  B1,
  input  B0,
  output O7,
  output O6,
  output O5,
  output O4,
  output O3,
  output O2,
  output O1,
  output O0,
  output AEq,
  output AGreater,
  output AZero
);

  wire [7:0] add_1_s, sub_1_s;

  Add #(.Bits(8)) add_1 (
    .a({A7, A6, A5, A4, A3, A2, A1, A0}), .b({B7, B6, B5, B4, B3, B2, B1, B0}), .c_i(1'b0), .s(add_1_s));  // open: c_o
  Sub #(.Bits(8)) sub_1 (
    .a({A7, A6, A5, A4, A3, A2, A1, A0}), .b({B7, B6, B5, B4, B3, B2, B1, B0}), .c_i(1'b0), .s(sub_1_s));  // open: c_o
  Multiplexer #(.Bits(8)) multiplexer_1 (
    .sel(Sub), .in_0(add_1_s), .in_1(sub_1_s), .out({O7, O6, O5, O4, O3, O2, O1, O0}));
  Comparator #(.Bits(8)) comparator_1 (
    .a({A7, A6, A5, A4, A3, A2, A1, A0}), .b({8{1'b0}}), .eq(AZero));  // open: gt, lt
  Comparator #(.Bits(8)) comparator_2 (
    .a({A7, A6, A5, A4, A3, A2, A1, A0}), .b({B7, B6, B5, B4, B3, B2, B1, B0}), .gt(AGreater), .eq(AEq));  // open: lt
endmodule
