// Digital circuit CPU.dig as structural Verilog
module CPU (
  input  clk,
  input  clk_2,
  input  InspectMode,
  input  [4:0] InspectAddr
);

  wire AEq, AGreater, alu_1_p26, alu_1_p27, alu_1_p28, ALUOut, and_1_out, and_2_out, and_3_out, and_4_out,
       AZero, clock_with_enable_1_clko, EnA, EnB, EnGnd, EnInst, hex_display_decoder_1_a,
       hex_display_decoder_1_b, hex_display_decoder_1_c, hex_display_decoder_1_d, hex_display_decoder_1_dp,
       hex_display_decoder_1_e, hex_display_decoder_1_f, hex_display_decoder_1_g, hex_display_decoder_2_a,
       hex_display_decoder_2_b, hex_display_decoder_2_c, hex_display_decoder_2_d, hex_display_decoder_2_dp,
       hex_display_decoder_2_e, hex_display_decoder_2_f, hex_display_decoder_2_g, Hlt, LdA, LdB, LdFlags,
       LdInst, LdMAddr, LdOut, MAddr_q5, MAddr_q6, MAddr_q7, MEn, MWr, not_2_out, not_3_out, not_4_out,
       or_1_out, or_2_out, or_3_out, PCClear, PCEnable, PCLd, PCOut, PrMode, Rdy, RegOut_q0, RegOut_q1,
       RegOut_q2, RegOut_q3, RegOut_q4, RegOut_q5, RegOut_q6, RegOut_q7, Reset_out, RstDone, StkDec, StkEn,
       StkInc, StkLd, StkRst, Sub, xor_1_out;
  wire [4:0] MAddr_q0, multiplexer_1_out, PrAddr;
  wire [7:0] A_q7, alu_1_p18, B_q7, counterpreset_1_out, driver_1_out, Inst_q7, multiplexer_2_out, PrData,
       stack_register_1_q;

  and and_1 (and_1_out, Rdy, RstDone);
  xor xor_1 (xor_1_out, and_2_out, RstDone);
  and and_2 (and_2_out, clk_2, PrMode);
  Counter #(.Bits(5)) counter_1 (.en(1'b1), .C(xor_1_out), .clr(and_1_out), .out(PrAddr), .ovf(Rdy));
  not not_1 (PrMode, Rdy);
  Button Reset (.out(Reset_out));
  LED READY (.in(Rdy));
  control_logic control_logic_1 (
    .Clk(not_3_out), .Inst(Inst_q7), .AEq(AEq), .AGreater(AGreater), .AZero(AZero), .Reset(Reset_out),
    .PCOut(PCOut), .PCEnable(PCEnable), .PCClear(PCClear), .PCLd(PCLd), .ALUOut(ALUOut), .LdOut(LdOut),
    .LdA(LdA), .EnA(EnA), .LdB(LdB), .EnB(EnB), .Sub(Sub), .LdInst(LdInst), .EnInst(EnInst),
    .LdMAddr(LdMAddr), .MWr(MWr), .MEn(MEn), .Hlt(Hlt), .LdFlags(LdFlags), .EnGnd(EnGnd), .RstDone(RstDone),
    .StkEn(StkEn), .StkLd(StkLd), .StkInc(StkInc), .StkDec(StkDec), .StkRst(StkRst));
  ROM #(.AddrBits(5), .isProgramMemory("true"), .Bits(8)) rom_1 (.A(PrAddr), .sel(1'b1), .D(PrData));
  clock_with_enable clock_with_enable_1 (.ClkI(clk), .En(Rdy), .ClkO(clock_with_enable_1_clko));
  not not_2 (not_2_out, Hlt);
  or or_1 (or_1_out, MWr, PrMode);
  and and_3 (and_3_out, not_2_out, clock_with_enable_1_clko);
  not not_3 (not_3_out, and_3_out);
  _8_bit_reg A (
    .Load(LdA), .Clk(and_3_out), .D7(driver_1_out[7]), .D6(driver_1_out[6]), .D5(driver_1_out[5]),
    .D4(driver_1_out[4]), .D3(driver_1_out[3]), .D2(driver_1_out[2]), .D1(driver_1_out[1]),
    .D0(driver_1_out[0]), .Q7(A_q7[7]), .Q6(A_q7[6]), .Q5(A_q7[5]), .Q4(A_q7[4]), .Q3(A_q7[3]), .Q2(A_q7[2]),
    .Q1(A_q7[1]), .Q0(A_q7[0]));
  _8_bit_reg B (
    .Load(LdB), .Clk(and_3_out), .D7(driver_1_out[7]), .D6(driver_1_out[6]), .D5(driver_1_out[5]),
    .D4(driver_1_out[4]), .D3(driver_1_out[3]), .D2(driver_1_out[2]), .D1(driver_1_out[1]),
    .D0(driver_1_out[0]), .Q7(B_q7[7]), .Q6(B_q7[6]), .Q5(B_q7[5]), .Q4(B_q7[4]), .Q3(B_q7[3]), .Q2(B_q7[2]),
    .Q1(B_q7[1]), .Q0(B_q7[0]));
  _8_bit_reg Inst (
    .Load(LdInst), .Clk(and_3_out), .D7(driver_1_out[7]), .D6(driver_1_out[6]), .D5(driver_1_out[5]),
    .D4(driver_1_out[4]), .D3(driver_1_out[3]), .D2(driver_1_out[2]), .D1(driver_1_out[1]),
    .D0(driver_1_out[0]), .Q7(Inst_q7[7]), .Q6(Inst_q7[6]), .Q5(Inst_q7[5]), .Q4(Inst_q7[4]),
    .Q3(Inst_q7[3]), .Q2(Inst_q7[2]), .Q1(Inst_q7[1]), .Q0(Inst_q7[0]));
  not not_4 (not_4_out, PrMode);
  and and_4 (and_4_out, not_4_out, MEn);
  assign driver_1_out = EnA ? A_q7 : 8'bz;  // Driver driver_1
  assign driver_1_out = EnB ? B_q7 : 8'bz;  // Driver driver_2
  assign driver_1_out = EnInst ? Inst_q7 : 8'bz;  // Driver driver_3
  or or_2 (or_2_out, and_3_out, and_2_out);
  assign driver_1_out = ALUOut ? alu_1_p18 : 8'bz;  // Driver driver_4
  assign driver_1_out = EnGnd ? {8{1'b0}} : 8'bz;  // Driver driver_5
  assign driver_1_out = PCOut ? counterpreset_1_out : 8'bz;  // Driver driver_6
  Multiplexer #(.Selector_Bits(2), .Bits(5)) multiplexer_1 (
    .sel({InspectMode, PrMode}), .in_0(MAddr_q0), .in_1(PrAddr), .in_2(InspectAddr), .in_3({5{1'b0}}),
    .out(multiplexer_1_out));
  _8_bit_reg RegOut (
    .Load(LdOut), .Clk(and_3_out), .D7(driver_1_out[7]), .D6(driver_1_out[6]), .D5(driver_1_out[5]),
    .D4(driver_1_out[4]), .D3(driver_1_out[3]), .D2(driver_1_out[2]), .D1(driver_1_out[1]),
    .D0(driver_1_out[0]), .Q7(RegOut_q7), .Q6(RegOut_q6), .Q5(RegOut_q5), .Q4(RegOut_q4), .Q3(RegOut_q3),
    .Q2(RegOut_q2), .Q1(RegOut_q1), .Q0(RegOut_q0));
  or or_3 (or_3_out, and_4_out, InspectMode);
  hex_display_decoder hex_display_decoder_1 (
    ._3(RegOut_q7), ._2(RegOut_q6), ._1(RegOut_q5), ._0(RegOut_q4), .A(hex_display_decoder_1_a),
    .B(hex_display_decoder_1_b), .C(hex_display_decoder_1_c), .D(hex_display_decoder_1_d),
    .E(hex_display_decoder_1_e), .F(hex_display_decoder_1_f), .G(hex_display_decoder_1_g),
    .DP(hex_display_decoder_1_dp));
  _32_byte_ram _32_byte_ram_1 (
    .Bus(multiplexer_2_out), .Addr(multiplexer_1_out), .Wr(or_1_out), .Clk(or_2_out), .En(or_3_out),
    .Out(driver_1_out));
  // ALU alu_1: pin names not known; wires that end beside it: Sub, A_q7[7], A_q7[6], A_q7[5], A_q7[4], A_q7[3], A_q7[2], A_q7[1], A_q7[0], B_q7[7], B_q7[6], B_q7[5], B_q7[4], B_q7[3], B_q7[2], B_q7[1], B_q7[0], alu_1_p18[7], alu_1_p18[6], alu_1_p18[5], alu_1_p18[4], alu_1_p18[3], alu_1_p18[2], alu_1_p18[1], alu_1_p18[0], alu_1_p26, alu_1_p27, alu_1_p28
  CounterPreset #(.Bits(8)) counterpreset_1 (
    .en(PCEnable), .C(and_3_out), .dir(1'b0), .in(driver_1_out), .ld(PCLd), .clr(PCClear),
    .out(counterpreset_1_out));  // open: ovf
  _8_bit_reg MAddr (
    .Load(LdMAddr), .Clk(and_3_out), .D7(driver_1_out[7]), .D6(driver_1_out[6]), .D5(driver_1_out[5]),
    .D4(driver_1_out[4]), .D3(driver_1_out[3]), .D2(driver_1_out[2]), .D1(driver_1_out[1]),
    .D0(driver_1_out[0]), .Q7(MAddr_q7), .Q6(MAddr_q6), .Q5(MAddr_q5), .Q4(MAddr_q0[4]), .Q3(MAddr_q0[3]),
    .Q2(MAddr_q0[2]), .Q1(MAddr_q0[1]), .Q0(MAddr_q0[0]));
  Seven_Seg seven_seg_1 (
    .a(hex_display_decoder_1_a), .b(hex_display_decoder_1_b), .c(hex_display_decoder_1_c),
    .d(hex_display_decoder_1_d), .e(hex_display_decoder_1_e), .f(hex_display_decoder_1_f),
    .g(hex_display_decoder_1_g), .dp(hex_display_decoder_1_dp));
  Multiplexer #(.Bits(8)) multiplexer_2 (.sel(PrMode), .in_0(driver_1_out), .in_1(PrData), .out(multiplexer_2_out));
  _8_bit_reg Flags (
    .Load(LdFlags), .Clk(and_3_out), .D7(1'b0), .D6(1'b0), .D5(1'b0), .D4(1'b0), .D3(1'b0), .D2(alu_1_p28),
    .D1(alu_1_p27), .D0(alu_1_p26), .Q2(AEq), .Q1(AGreater), .Q0(AZero));  // open: Q7, Q6, Q5, Q4, Q3
  Seven_Seg seven_seg_2 (
    .a(hex_display_decoder_2_a), .b(hex_display_decoder_2_b), .c(hex_display_decoder_2_c),
    .d(hex_display_decoder_2_d), .e(hex_display_decoder_2_e), .f(hex_display_decoder_2_f),
    .g(hex_display_decoder_2_g), .dp(hex_display_decoder_2_dp));
  hex_display_decoder hex_display_decoder_2 (
    ._3(RegOut_q3), ._2(RegOut_q2), ._1(RegOut_q1), ._0(RegOut_q0), .A(hex_display_decoder_2_a),
    .B(hex_display_decoder_2_b), .C(hex_display_decoder_2_c), .D(hex_display_decoder_2_d),
    .E(hex_display_decoder_2_e), .F(hex_display_decoder_2_f), .G(hex_display_decoder_2_g),
    .DP(hex_display_decoder_2_dp));
  stack_register stack_register_1 (
    .Ld(StkLd), .Clk(and_3_out), .Inc(StkInc), .Dec(StkDec), .Rst(StkRst), .D(driver_1_out),
    .Q(stack_register_1_q));
  assign driver_1_out = StkEn ? stack_register_1_q : 8'bz;  // Driver driver_7

  // Notes on the sheet:
  //   clk: Hz: 50
  //   clk_2: Hz: 50
  //   contents of rom_1 (hex, n*v repeats v):
  //   1,a,2,16,1e,1f,4*0,14
endmodule
