// Digital circuit HexOut.dig as structural Verilog
module HexOut (
);

  Seven_Seg seven_seg_1 ();  // open: a, b, c, d, e, f, g, dp
  Seven_Seg seven_seg_2 ();  // open: a, b, c, d, e, f, g, dp
endmodule
