// Digital circuit control_logic.dig as structural Verilog
module control_logic (
  input  Clk,
  input  [7:0] Inst,
  input  AEq,
  input  AGreater,
  input  AZero,
  input  Reset,
  output PCOut,
  output PCEnable,
  output PCClear,
  output PCLd,
  output ALUOut,
  output LdOut,
  output LdA,
  output EnA,
  output LdB,
  output EnB,
  output Sub,
  output LdInst,
  output EnInst,
  output LdMAddr,
  output MWr,
  output MEn,
  output Hlt,
  output LdFlags,
  output EnGnd,
  output RstDone,
  output StkEn,
  output StkLd,
  output StkInc,
  output StkDec,
  output StkRst
);

  wire and_1_out, and_2_out, and_3_out, d_ff_1_q, or_1_out, or_2_out, or_3_out;
  wire [1:0] rom_3_d;
  wire [2:0] counter_1_out, rom_2_d_2;
  wire [7:0] multiplexer_1_out, rom_1_d;
  wire [20:3] rom_2_d;

  ROM #(.AddrBits(1), .Bits(8)) rom_1 (.A(1'b0), .sel(1'b1), .D(rom_1_d));
  or or_1 (or_1_out, Reset, RstDone);
  or or_2 (or_2_out, rom_2_d[20], Reset);
  D_FF d_ff_1 (.D(Reset), .C(or_1_out), .Q(d_ff_1_q));  // open: nQ
  or or_3 (or_3_out, AGreater, AEq);
  Counter #(.Bits(3)) counter_1 (.en(1'b1), .C(Clk), .clr(or_2_out), .out(counter_1_out));  // open: ovf
  Multiplexer #(.Bits(8)) multiplexer_1 (.sel(d_ff_1_q), .in_0(Inst), .in_1(rom_1_d), .out(multiplexer_1_out));
  ROM #(.AddrBits(8), .isProgramMemory("true"), .Bits(29)) rom_2 (
    .A({multiplexer_1_out[4:0], counter_1_out}), .sel(1'b1),
    .D({StkRst, StkDec, StkInc, StkLd, StkEn, rom_2_d_2, rom_2_d[20], RstDone, EnGnd, LdFlags, Hlt, MEn, MWr, LdMAddr, EnInst, LdInst, Sub, EnB, LdB, EnA, LdA, LdOut, ALUOut, rom_2_d[3], PCClear, PCEnable, PCOut}));
  and and_1 (and_1_out, rom_2_d[3], AEq);
  and and_2 (and_2_out, rom_2_d[3], or_3_out);
  and and_3 (and_3_out, rom_2_d[3], AZero);
  ROM #(.AddrBits(3), .Bits(2)) rom_3 (.A(rom_2_d_2), .sel(1'b1), .D(rom_3_d));
  Multiplexer #(.Selector_Bits(2)) multiplexer_2 (
    .sel(rom_3_d), .in_0(rom_2_d[3]), .in_1(and_1_out), .in_2(and_2_out), .in_3(and_3_out), .out(PCLd));

  // Notes on the sheet:
  //   Reset impulse
  //   Reset done
  //   contents of rom_1 (hex, n*v repeats v):
  //   1d
  //   // Ignore the 3 high bits, reserved for the microcode counter
  //   rom_2 loads rom.hex
  //   PcLdIfGorEq
  //   PCLdIfZero
  //   MPCRst
  //   PCLdIfEq
  //   If Equal
  //   If Greater or Equal
  //   If Zero
  //   contents of rom_3 (hex, n*v repeats v):
  //   0,1,2,0,3
endmodule
