// Digital circuit hex_display_decoder.dig as structural Verilog
module hex_display_decoder (
  input  _3,
  input  _2,
  input  _1,
  input  _0,
  output A,
  output B,
  output C,
  output D,
  output E,
  output F,
  output G,
  output DP
);

  ROM #(.AddrBits(4), .isProgramMemory("true"), .Bits(8)) rom_1 (
    .A({_3, _2, _1, _0}), .sel(1'b1), .D({A, B, C, D, E, F, G, DP}));
  Seven_Seg seven_seg_1 (.a(A), .b(B), .c(C), .d(D), .e(E), .f(F), .g(G), .dp(DP));

  // Notes on the sheet:
  //   contents of rom_1 (hex, n*v repeats v):
  //   fc,60,da,f2,66,b6,be,e0,fe,f6,ef,ff,9d,fd,9f,8f
endmodule
