// Digital circuit pc.dig as structural Verilog
module pc (
  input  clk,
  output O1,
  output O2,
  output O3,
  output O4,
  output O5,
  output O6,
  output O7,
  output O0
);

  wire jk_ff_1_q, jk_ff_2_q, jk_ff_3_q, jk_ff_4_q, jk_ff_5_q, jk_ff_6_q, jk_ff_7_q, jk_ff_8_q;

  JK_FF jk_ff_1 (.J(1'b1), .C(clk), .K(1'b1), .Q(jk_ff_1_q));  // open: nQ
  JK_FF jk_ff_2 (.J(1'b1), .C(jk_ff_1_q), .K(1'b1), .Q(jk_ff_2_q));  // open: nQ
  JK_FF jk_ff_3 (.J(1'b1), .C(jk_ff_2_q), .K(1'b1), .Q(jk_ff_3_q));  // open: nQ
  JK_FF jk_ff_4 (.J(1'b1), .C(jk_ff_3_q), .K(1'b1), .Q(jk_ff_4_q));  // open: nQ
  JK_FF jk_ff_5 (.J(1'b1), .C(jk_ff_4_q), .K(1'b1), .Q(jk_ff_5_q));  // open: nQ
  JK_FF jk_ff_6 (.J(1'b1), .C(jk_ff_5_q), .K(1'b1), .Q(jk_ff_6_q));  // open: nQ
  JK_FF jk_ff_7 (.J(1'b1), .C(jk_ff_6_q), .K(1'b1), .Q(jk_ff_7_q));  // open: nQ
  JK_FF jk_ff_8 (.J(1'b1), .C(jk_ff_7_q), .K(1'b1), .Q(jk_ff_8_q));  // open: nQ
  not not_1 (O0, jk_ff_1_q);
  not not_2 (O1, jk_ff_2_q);
  not not_3 (O2, jk_ff_3_q);
  not not_4 (O3, jk_ff_4_q);
  not not_5 (O4, jk_ff_5_q);
  not not_6 (O5, jk_ff_6_q);
  not not_7 (O6, jk_ff_7_q);
  not not_8 (O7, jk_ff_8_q);
endmodule
