// Digital circuit sr_latch_en.dig as structural Verilog
module sr_latch_en (
  input  R,
  input  Enable,
  input  S,
  output Q,
  output Q_2
);

  wire and_1_out, and_2_out;

  and and_1 (and_1_out, R, Enable);
  and and_2 (and_2_out, Enable, S);
  nor nor_1 (Q, and_1_out, Q_2);
  nor nor_2 (Q_2, Q, and_2_out);
endmodule
