// Digital circuit stack_register.dig as structural Verilog
module stack_register (
  input  Ld,
  input  Clk,
  input  Inc,
  input  Dec,
  input  Rst,
  input  [7:0] D,
  output [7:0] Q
);

  wire d_ff_1_nq, or_1_out, or_2_out;
  wire [7:0] _8_bit_reg_1_q7, add_1_s, multiplexer_1_out, rom_1_d, sub_1_s;

  D_FF d_ff_1 (.D(1'b1), .C(Clk), .nQ(d_ff_1_nq));  // open: Q
  or or_1 (or_1_out, Rst, d_ff_1_nq);
  Multiplexer #(.Bits(8)) multiplexer_1 (.sel(or_1_out), .in_0(D), .in_1({8{1'b1}}), .out(multiplexer_1_out));
  or or_2 (or_2_out, or_1_out, Ld);
  _8_bit_reg _8_bit_reg_1 (
    .Load(or_2_out), .Clk(Clk), .D7(multiplexer_1_out[7]), .D6(multiplexer_1_out[6]),
    .D5(multiplexer_1_out[5]), .D4(multiplexer_1_out[4]), .D3(multiplexer_1_out[3]),
    .D2(multiplexer_1_out[2]), .D1(multiplexer_1_out[1]), .D0(multiplexer_1_out[0]), .Q7(_8_bit_reg_1_q7[7]),
    .Q6(_8_bit_reg_1_q7[6]), .Q5(_8_bit_reg_1_q7[5]), .Q4(_8_bit_reg_1_q7[4]), .Q3(_8_bit_reg_1_q7[3]),
    .Q2(_8_bit_reg_1_q7[2]), .Q1(_8_bit_reg_1_q7[1]), .Q0(_8_bit_reg_1_q7[0]));
  ROM #(.AddrBits(1), .Bits(8)) rom_1 (.A(1'b0), .sel(1'b1), .D(rom_1_d));
  Sub #(.Bits(8)) sub_1 (.a(_8_bit_reg_1_q7), .b(rom_1_d), .c_i(1'b0), .s(sub_1_s));  // open: c_o
  Add #(.Bits(8)) add_1 (.a(_8_bit_reg_1_q7), .b(rom_1_d), .c_i(1'b0), .s(add_1_s));  // open: c_o
  Multiplexer #(.Selector_Bits(2), .Bits(8)) multiplexer_2 (
    .sel({Inc, Dec}), .in_0(_8_bit_reg_1_q7), .in_1(sub_1_s), .in_2(add_1_s), .in_3({8{1'b0}}), .out(Q));

  // Notes on the sheet:
  //   contents of rom_1 (hex, n*v repeats v):
  //   1
endmodule
