// Digital circuit test.dig as structural Verilog
module test (
  input  First,
  input  Second,
  output out_3,
  output out_4
);

  half_adder half_adder_1 (.A(First), .B(Second), .S(out_3), .C(out_4));
endmodule
